# Fritzing sketch L293D_Breadbord - 2 motors and ultrasonic-sensor (saved by Fritzing 1.0.4)
breadboards: 1

parts:
  IC1 = L293D [package=THT]
  Mod1 = Raspberry Pi 4B
  VCC1 = Battery block 9V [internal_resistance=0.1Ω]
  M1 = DC Motor [voltage_(max)=6V voltage_(min)=3V]
  M2 = DC Motor [voltage_(max)=6V voltage_(min)=3V]
  HC-SR04_Sensor_1 = HC-SR04 Ultrasonic Distance Sensor
  R1 = Resistor [tolerance=±5% power=0.25W resistance=1000 package=THT]
  R2 = Resistor [tolerance=±5% power=0.25W resistance=1000 package=THT]
  R3 = Resistor [tolerance=±5% power=0.25W resistance=1000 package=THT]
  HC-SR04_Sensor_2 = HC-SR04 Ultrasonic Distance Sensor
  HC-SR04_Sensor_3 = HC-SR04 Ultrasonic Distance Sensor
  R4 = Resistor [tolerance=±5% power=0.25W resistance=2000 package=THT]
  R5 = Resistor [tolerance=±5% power=0.25W resistance=2000 package=THT]
  R6 = Resistor [tolerance=±5% power=0.25W resistance=2000 package=THT]
  R7 = Resistor [tolerance=±5% power=0.25W resistance=1000 package=THT]  # not connected

nets:
  N1: IC1.Enable_1, IC1.Enable_2, IC1.+V, Mod1.5V
  N2: IC1.In_1, Mod1.GPIO23
  N3: IC1.Out_1_(_Controlled_by_Enable_1_), M2.pin_2
  GND: IC1.0V, Mod1.GND, VCC1.-, HC-SR04_Sensor_1.GND, HC-SR04_Sensor_2.GND, HC-SR04_Sensor_3.GND, R4.Pin_1, R5.Pin_1, R6.Pin_1
  N4: IC1.Out_2_(_Controlled_by_Enable_1_), M2.pin_1
  N5: IC1.In_2, Mod1.GPIO24
  N6: IC1.+Vmotor, VCC1.+
  N7: IC1.In_3, Mod1.GPIO27
  N8: IC1.Out_3_(_Controlled_by_Enable_2_), M1.pin_2
  N9: IC1.Out_4_(_Controlled_by_Enable_2_), M1.pin_1
  N10: IC1.In_4, Mod1.GPIO22
  N11: Mod1.GPIO5, HC-SR04_Sensor_2.TRIG
  N12: Mod1.GPIO6, R3.Pin_1, R6.Pin_0
  N13: Mod1.GPIO12, HC-SR04_Sensor_1.TRIG
  N14: Mod1.GPIO19, HC-SR04_Sensor_3.TRIG
  N15: Mod1.GPIO16, R1.Pin_1, R4.Pin_0
  N16: Mod1.GPIO26, R2.Pin_1, R5.Pin_0
  VCC: HC-SR04_Sensor_1.VCC, HC-SR04_Sensor_2.VCC, HC-SR04_Sensor_3.VCC
  N17: HC-SR04_Sensor_1.ECHO, R1.Pin_0
  N18: R2.Pin_0, HC-SR04_Sensor_2.ECHO
  N19: R3.Pin_0, HC-SR04_Sensor_3.ECHO
