# Fritzing sketch L293D_Breadbord - Kopie (saved by Fritzing 1.0.4)
breadboards: 1

parts:
  IC1 = L293D [package=THT]
  Mod1 = Raspberry Pi 4B
  M1 = DC Motor [voltage_(max)=6V voltage_(min)=3V]
  VCC1 = Battery block 9V [internal_resistance=0.1Ω]

nets:
  N1: IC1.Enable_1, IC1.+V, Mod1.5V
  N2: IC1.In_1, Mod1.GPIO12
  N3: IC1.Out_1_(_Controlled_by_Enable_1_), M1.pin_2
  N4: IC1.0V, IC1.In_2, Mod1.GND, VCC1.-
  N5: IC1.Out_2_(_Controlled_by_Enable_1_), M1.pin_1
  N6: IC1.+Vmotor, VCC1.+
