# Fritzing sketch Untitled Sketch 2 (saved by Fritzing 1.0.4)
breadboards: 2

parts:
  IC1 = L293D [package=THT]
  Mod1 = Raspberry Pi 4B
  M1 = DC Motor [voltage_(max)=6V voltage_(min)=3V]
  M3 = DC Motor [voltage_(max)=6V voltage_(min)=3V]
  VCC1 = Battery block 9V [internal_resistance=0.1Ω]
  Bauteil1 = Arduino Uno (Rev3)
  IC2 = L293D [package=THT]
  M4 = DC Motor [voltage_(max)=6V voltage_(min)=3V]
  M5 = DC Motor [voltage_(max)=6V voltage_(min)=3V]
  VCC2 = 4 x AAA Battery Mount [internal_resistance=0.1Ω]

nets:
  N1: IC1.Enable_1, Mod1.GPIO2
  N2: IC1.Out_1_(_Controlled_by_Enable_1_), M1.pin_2
  N3: IC1.0V, Mod1.GND, VCC1.-
  N4: IC1.Out_2_(_Controlled_by_Enable_1_), M1.pin_1
  N5: IC1.In_2, Mod1.GPIO3
  N6: IC1.+Vmotor, Mod1.5V, VCC1.+
  N7: IC1.In_3, Mod1.GPIO4
  N8: IC1.Out_3_(_Controlled_by_Enable_2_), M3.pin_2
  N9: IC1.Out_4_(_Controlled_by_Enable_2_), M3.pin_1
  N10: IC1.In_4, Mod1.GPIO23
  N11: Bauteil1.GND, IC2.Enable_1, IC2.0V, VCC2.-
  N12: Bauteil1.D2, IC2.In_1
  N13: Bauteil1.5V, IC2.Enable_2, IC2.+V
  N14: IC2.Out_1_(_Controlled_by_Enable_1_), M5.pin_1
  N15: IC2.Out_2_(_Controlled_by_Enable_1_), M5.pin_2
  N16: IC2.+Vmotor, VCC2.+
  N17: IC2.Out_3_(_Controlled_by_Enable_2_), M4.pin_2
  N18: IC2.Out_4_(_Controlled_by_Enable_2_), M4.pin_1
