# Fritzing sketch fanmotorMitL293ohneBatterie (saved by Fritzing 0.9.9b)
breadboards: 1

parts:
  IC1 = L293D [package=THT]
  M1 = DC Motor
  Mod1 = Raspberry Pi 4B
  R1 = Resistor [tolerance=±5% resistance=4.7k package=THT]

nets:
  N1: IC1.Enable_1, Mod1.GPIO18, R1.Pin_1
  N2: IC1.In_1, IC1.+Vmotor, IC1.+V, Mod1.5V
  N3: IC1.Out_1_(_Controlled_by_Enable_1_), IC1.Out_2_(_Controlled_by_Enable_1_), M1.pin_1, M1.pin_2
  GND: IC1.0V, IC1.In_2, IC1.Enable_2, IC1.In_3, IC1.In_4, Mod1.GND
  N4: Mod1.3V3, R1.Pin_0
